// Logisim project 8051.circ as structural Verilog
module ALU (
  input  CarryIn,
  input  [7:0] Accumulator,
  input  [7:0] RegisterB,
  input  [2:0] Opcode,
  output CarryFlag,
  output [7:0] out_6
);

  wire multiplexer_1_out;
  wire [7:0] multiplexer_2_out, negator_1_out;

  Negator negator_1 (.in(RegisterB), .out(negator_1_out));
  Multiplexer multiplexer_1 (.in0(1'b0), .in1(CarryIn), .out(multiplexer_1_out), .sel(Opcode[2]));
  Multiplexer #(.select(3), .width(8)) multiplexer_2 (
    .in0(8'h1), .in1({8{1'b1}}), .in2(RegisterB), .in3(negator_1_out), .out(multiplexer_2_out), .sel(Opcode));  // open: in4, in5, in6, in7
  Adder adder_1 (.a(Accumulator), .b(multiplexer_2_out), .out(out_6), .cin(multiplexer_1_out));  // open: cout

  // Notes on the sheet:
  //   -1
endmodule
